# Fritzing sketch watering-robot (saved by Fritzing 0.8.7b)
breadboards: 1

parts:
  Raspberry_Pi_A1 = Raspberry Pi A
  パーツ1 = Arduino Uno (Rev3) - ICSP
  RHT1 = Humidity and Temperature Sensor RHT03  # not connected
  U1 = mystery part, 3 pins [chip_label=Moist]

nets:
  5V: Raspberry_Pi_A1.5V, パーツ1.5V, U1.pin2
  GND: Raspberry_Pi_A1.GND, パーツ1.GND, U1.pin1
  N1: パーツ1.A0, U1.pin3
